// Logisim project UShiftReg.circ as structural Verilog: 1 circuit, main circuit main
module main (
  input  BitShiftRight,
  input  A7,
  input  A6,
  input  A5,
  input  A4,
  input  A3,
  input  A2,
  input  A1,
  input  BitShiftLeft,
  input  A0,
  input  Reset,
  input  [1:0] Selector,
  output out_13,
  output out_14,
  output out_15,
  output out_16,
  output out_17,
  output out_18,
  output out_19,
  output out_20
);

  wire Cloci_out, multiplexer_1_out, multiplexer_2_out, multiplexer_3_out, multiplexer_4_out,
       multiplexer_5_out, multiplexer_6_out, multiplexer_7_out, multiplexer_8_out;

  Multiplexer #(.select(2)) multiplexer_1 (
    .in0(out_19), .in1(out_18), .in2(out_20), .in3(A1), .out(multiplexer_1_out), .sel(Selector));
  Multiplexer #(.select(2)) multiplexer_2 (
    .in0(out_20), .in1(out_19), .in2(BitShiftLeft), .in3(A0), .out(multiplexer_2_out), .sel(Selector));
  Multiplexer #(.select(2)) multiplexer_3 (
    .in0(out_13), .in1(BitShiftRight), .in2(out_14), .in3(A7), .out(multiplexer_3_out), .sel(Selector));
  Multiplexer #(.select(2)) multiplexer_4 (
    .in0(out_14), .in1(out_13), .in2(out_15), .in3(A6), .out(multiplexer_4_out), .sel(Selector));
  Multiplexer #(.select(2)) multiplexer_5 (
    .in0(out_15), .in1(out_14), .in2(out_16), .in3(A5), .out(multiplexer_5_out), .sel(Selector));
  Multiplexer #(.select(2)) multiplexer_6 (
    .in0(out_16), .in1(out_15), .in2(out_17), .in3(A4), .out(multiplexer_6_out), .sel(Selector));
  Multiplexer #(.select(2)) multiplexer_7 (
    .in0(out_17), .in1(out_16), .in2(out_18), .in3(A3), .out(multiplexer_7_out), .sel(Selector));
  Multiplexer #(.select(2)) multiplexer_8 (
    .in0(out_18), .in1(out_17), .in2(out_19), .in3(A2), .out(multiplexer_8_out), .sel(Selector));
  Clock Cloci (.out(Cloci_out));
  D_Flip_Flop d_ff_1 (.D(multiplexer_3_out), .clk(Cloci_out), .Q(out_13), .reset(Reset));  // open: Qn, preset
  D_Flip_Flop d_ff_2 (.D(multiplexer_4_out), .clk(Cloci_out), .Q(out_14), .reset(Reset));  // open: Qn, preset
  D_Flip_Flop d_ff_3 (.D(multiplexer_5_out), .clk(Cloci_out), .Q(out_15), .reset(Reset));  // open: Qn, preset
  D_Flip_Flop d_ff_4 (.D(multiplexer_6_out), .clk(Cloci_out), .Q(out_16), .reset(Reset));  // open: Qn, preset
  D_Flip_Flop d_ff_5 (.D(multiplexer_7_out), .clk(Cloci_out), .Q(out_17), .reset(Reset));  // open: Qn, preset
  D_Flip_Flop d_ff_6 (.D(multiplexer_8_out), .clk(Cloci_out), .Q(out_18), .reset(Reset));  // open: Qn, preset
  D_Flip_Flop d_ff_7 (.D(multiplexer_1_out), .clk(Cloci_out), .Q(out_19), .reset(Reset));  // open: Qn, preset
  D_Flip_Flop d_ff_8 (.D(multiplexer_2_out), .clk(Cloci_out), .Q(out_20), .reset(Reset));  // open: Qn, preset
endmodule
